# Fritzing sketch Diagram (saved by Fritzing 1.0.2b)

parts:
  Mod1 = Raspberry Pi Pico
  LED1 = LEDs [package=led10mm]
  LED2 = LEDs [package=led10mm]
  LED3 = LEDs [package=led10mm]
  LED4 = LEDs [package=led10mm]
  LED5 = LEDs [package=led10mm]
  LED6 = LEDs [package=led10mm]
  LED7 = LEDs [package=led10mm]
  LED8 = LEDs [package=led10mm]
  LED9 = LEDs [package=led10mm]
  S1 = Square Pushbutton
  BAT1 = Battery Holders [package=battery-aa-panel]
  S2 = Square Pushbutton

nets:
  N1: Mod1.pin_23, Mod1.pin_33, LED1.C, LED2.C, LED3.C, LED4.C, LED5.C, LED6.C, LED7.C, LED8.C, LED9.C, S1.leg1, BAT1.-
  N2: Mod1.pin_24, LED7.A, LED8.A
  N3: Mod1.pin_25, LED4.A, LED5.A
  N4: Mod1.pin_26, LED1.A, LED3.A
  N5: Mod1.pin_27, S1.leg0
  N6: Mod1.pin_37, S2.leg0
  N7: BAT1.+, S2.leg1

custom parts:
  Raspberry Pi Pico: Raspberry Pi Pico. Based around the RP2040 microcontroller the Pico is a low cost microcontroller device bringing Raspberry Pi quality, cost, and easy of use to the microcontroller space. Jan 2021, Split part in to two versions: tht (this one) and SMD. This one will drill holes for a .1 in header in pcb to allow plugging in the module as well as providing pads to solder the module to the top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
